// Digital circuit JK-circuit.dig as structural Verilog
module JK_circuit (
  input  X,
  input  C,
  output Z
);

  wire and_1_out, and_2_out, and_3_out, and_4_out, and_5_out, and_6_out, and_7_out, and_8_out, and_9_out,
       and_10_out, and_11_out, not_1_out, not_2_out, not_3_out, not_4_out, or_1_out, or_2_out, or_3_out,
       or_4_out, Z_0_n, Z_1_n, Z_2_n;

  not not_1 (not_1_out, X);
  not not_2 (not_2_out, Z_2_n);
  not not_3 (not_3_out, Z_1_n);
  not not_4 (not_4_out, Z_0_n);
  and and_1 (and_1_out, not_1_out, Z_1_n);
  and and_2 (and_2_out, not_1_out, not_4_out, Z_1_n);
  and and_3 (and_3_out, X, not_3_out);
  and and_4 (and_4_out, X, Z_0_n);
  or or_1 (or_1_out, X, Z_2_n);
  and and_5 (and_5_out, X, Z_1_n);
  and and_6 (and_6_out, not_3_out, not_2_out);
  and and_7 (and_7_out, Z_1_n, Z_2_n);
  and and_8 (and_8_out, not_1_out, Z_2_n);
  and and_9 (and_9_out, X, not_3_out);
  and and_10 (and_10_out, not_4_out, not_3_out, Z_2_n);
  and and_11 (and_11_out, Z_0_n, Z_1_n, Z_2_n);
  or or_2 (or_2_out, and_2_out, and_3_out, and_4_out);
  or or_3 (or_3_out, and_5_out, and_6_out, and_7_out);
  or or_4 (or_4_out, and_8_out, and_9_out);
  or or_5 (Z, and_10_out, and_11_out);
  JK_FF u_Z_2_n (.J(and_1_out), .C(C), .K(or_2_out), .Q(Z_2_n));  // open: nQ
  JK_FF u_Z_1_n (.J(or_1_out), .C(C), .K(not_1_out), .Q(Z_1_n));  // open: nQ
  JK_FF u_Z_0_n (.J(or_3_out), .C(C), .K(or_4_out), .Q(Z_0_n));  // open: nQ
  // Probe state on {X, Z_2_n, Z_1_n, Z_0_n}

  // Notes on the sheet:
  //   C: Hz: 2
endmodule
