// Digital circuit mealy_NAND-circuit.dig as structural Verilog
module mealy_NAND_circuit (
  input  X,
  input  C,
  output Z
);

  wire nand_1_out, nand_2_out, nand_3_out, nand_4_out, nand_5_out, nand_6_out, nand_7_out, nand_8_out,
       nand_9_out, nand_10_out, nand_11_out, nand_12_out, nand_13_out, nand_14_out, nand_15_out, not_1_out,
       not_2_out, not_3_out, not_4_out, Z_0_n, Z_1_n, Z_2_n;

  not not_1 (not_1_out, X);
  not not_2 (not_2_out, Z_2_n);
  not not_3 (not_3_out, Z_1_n);
  not not_4 (not_4_out, Z_0_n);
  nand nand_1 (nand_1_out, X, Z_1_n, not_2_out);
  nand nand_2 (nand_2_out, X, not_3_out, Z_2_n);
  nand nand_3 (nand_3_out, Z_0_n, Z_1_n);
  nand nand_4 (nand_4_out, not_1_out, not_3_out);
  nand nand_5 (nand_5_out, X, Z_1_n, not_2_out);
  nand nand_6 (nand_6_out, not_1_out, not_4_out);
  nand nand_7 (nand_7_out, not_3_out, Z_2_n);
  nand nand_8 (nand_8_out, X, not_3_out, not_2_out);
  nand nand_9 (nand_9_out, Z_0_n, not_3_out);
  nand nand_10 (nand_10_out, Z_1_n, Z_2_n);
  nand nand_11 (nand_11_out, X, not_3_out, Z_2_n);
  nand nand_12 (nand_12_out, not_1_out, Z_1_n, Z_2_n);
  nand nand_13 (nand_13_out, nand_1_out, nand_2_out, nand_3_out);
  nand nand_14 (nand_14_out, nand_4_out, nand_5_out, nand_6_out, nand_7_out);
  nand nand_15 (nand_15_out, nand_8_out, nand_9_out, nand_10_out);
  nand nand_16 (Z, nand_11_out, nand_12_out);
  D_FF u_Z_2_n (.D(nand_13_out), .C(C), .Q(Z_2_n));  // open: nQ
  D_FF u_Z_1_n (.D(nand_14_out), .C(C), .Q(Z_1_n));  // open: nQ
  D_FF u_Z_0_n (.D(nand_15_out), .C(C), .Q(Z_0_n));  // open: nQ
  // Probe state on {X, Z_2_n, Z_1_n, Z_0_n}

  // Notes on the sheet:
  //   C: Hz: 2
endmodule
